// Digital circuit 2021-counter.dig as structural Verilog
module _2021_counter (
  input  in_1
);

  wire comparator_1_eq;
  wire [3:0] add_1_s, counter_1_out, div_1_q, div_1_r;
  wire [7:0] mul_1_mul;

  Counter #(.Bits(4)) counter_1 (.en(1'b1), .C(in_1), .clr(comparator_1_eq), .out(counter_1_out));  // open: ovf
  Add #(.Bits(4)) add_1 (.a(counter_1_out), .b(4'b0001), .c_i(1'b0), .s(add_1_s));  // open: c_o
  Comparator #(.Bits(4)) comparator_1 (.a(counter_1_out), .b(4'b0100), .eq(comparator_1_eq));  // open: gt, lt
  Mul #(.Bits(4)) mul_1 (.a(add_1_s), .b(4'b0011), .mul(mul_1_mul));
  Seven_Seg_Hex seven_seg_hex_1 (.d(mul_1_mul[3:0]), .dp(1'b0));
  Div #(.Bits(4)) div_1 (.a(mul_1_mul[3:0]), .b(4'b1010), .q(div_1_q), .r(div_1_r));
  Seven_Seg_Hex seven_seg_hex_2 (.d(div_1_q), .dp(1'b0));
  Seven_Seg_Hex seven_seg_hex_3 (.d(div_1_r), .dp(1'b0));
endmodule
