// Digital circuit 2023-counter.dig as structural Verilog
module _2023_counter (
  input  clk,
  input  reset,
  output C,
  output B,
  output A
);

  wire [2:0] counter_1_out;
  wire [3:3] multiplexer_1_out;

  Counter #(.Bits(3)) counter_1 (.en(1'b1), .C(clk), .clr(reset), .out(counter_1_out));  // open: ovf
  Multiplexer #(.Selector_Bits(3), .Bits(4)) multiplexer_1 (
    .sel(counter_1_out), .in_0(4'b0000), .in_1(4'b0010), .in_2(4'b0100), .in_3(4'b0001), .in_4(4'b0011),
    .in_5(4'b0110), .in_6(4'b0101), .in_7(4'b0111), .out({multiplexer_1_out[3], C, B, A}));
  // Probe on counter_1_out
  Seven_Seg_Hex seven_seg_hex_1 (.d({multiplexer_1_out[3], C, B, A}), .dp(1'b0));
endmodule

/* Test case TestCase:
clk reset C B A
0 0 0 0 0 
0 1 0 0 0
1 1 0 0 0
0 0 0 0 0
1 0 0 1 0
0 0 0 1 0
1 0 1 0 0
0 0 1 0 0 
1 0 0 0 1
0 0 0 0 1
1 0 0 1 1
0 0 0 1 1
1 0 1 1 0
0 0 1 1 0
1 0 1 0 1
0 0 1 0 1
1 0 1 1 1
0 0 1 1 1
1 0 0 0 0
0 0 0 0 0
1 0 0 1 0
0 0 0 1 0
1 0 1 0 0
0 0 1 0 0 
1 0 0 0 1
0 0 0 0 1
1 0 0 1 1
0 0 0 1 1
1 0 1 1 0
0 0 1 1 0
1 0 1 0 1
0 0 1 0 1
1 0 1 1 1
0 0 1 1 1
*/
