// Digital circuit 2023-second-largest.dig as structural Verilog
module _2023_second_largest (
  input  clk,
  input  \input ,
  input  [15:0] A,
  input  reset,
  output [15:0] max,
  output [15:0] second
);

  wire and_3_out, and_4_out, comparator_1_gt, comparator_2_gt, comparator_3_gt, d_ff_1_q, d_ff_2_q, inp,
       or_1_out, \reg , switch;
  wire [15:0] multiplexer_1_out;

  D_FF d_ff_1 (.D(\input ), .C(clk), .Q(d_ff_1_q));  // open: nQ
  Comparator #(.Bits(16)) comparator_1 (.a(A), .b(max), .gt(comparator_1_gt));  // open: eq, lt
  D_FF_AS #(.Bits(16)) d_ff_as_1 (.Set(1'b0), .D(A), .C(\reg ), .Clr(reset), .Q(max));  // open: nQ
  D_FF d_ff_2 (.D(d_ff_1_q), .C(clk), .Q(d_ff_2_q));  // open: nQ
  and and_1 (inp, d_ff_1_q, ~d_ff_2_q);  // And
  Comparator #(.Bits(16)) comparator_2 (.a(A), .b(max), .gt(comparator_2_gt));  // open: eq, lt
  and and_2 (\reg , inp, comparator_1_gt);
  and and_3 (and_3_out, inp, comparator_2_gt);
  Multiplexer #(.Bits(16)) multiplexer_1 (.sel(switch), .in_0(max), .in_1(A), .out(multiplexer_1_out));
  D_FF_AS #(.Bits(16)) d_ff_as_2 (
    .Set(1'b0), .D(multiplexer_1_out), .C(or_1_out), .Clr(reset), .Q(second));  // open: nQ
  Comparator #(.Bits(16)) comparator_3 (.a(A), .b(second), .gt(comparator_3_gt));  // open: eq, lt
  LookUpTable switch_sel (.in0(comparator_2_gt), .in1(comparator_3_gt), .out(switch));
  and and_4 (and_4_out, ~comparator_2_gt, inp, comparator_3_gt);  // And
  or or_1 (or_1_out, and_4_out, and_3_out);

  // Other names for the same wires on the sheet: rst = reset

  // Notes on the sheet:
  //   clk: Hz: 10
  //   Second Max
  //   A 16 bits
  //   input 1 bit
  //   reset 1 bit
  //   clk
  //   //output second largest number
  //   contents of switch_sel (hex, n*v repeats v):
  //   0,0,1
endmodule

/* Test case Case1:
clk A input reset second
0 0 0 0 0
1 0 0 0 0
0 0 0 1 0
1 0 0 1 0
0 0  0 0 0
1 0  0 0 0
0 5 1 0 X
1 5 1 0 X
0  0 0 0 0
1  0 0 0 0
0 12 1 0 X
1 12 1 0 X
0  0 0 0 X
1  0 0 0 5
*/

/* Test case Case2:
clk A input reset second
0 0 0 0 0
1 0 0 0 0
0 0 0 1 0
1 0 0 1 0
0 0  0 0 0
1 0  0 0 0
0 5 1 0 X
1 5 1 0 X
0  0 0 0 0
1  0 0 0 0
0 15 1 0 X
1 15 1 0 X
0  0 0 0 X
1  0 0 0 5
*/

/* Test case Case3:
clk A input reset second
0 0 0 0 0
1 0 0 0 0
0 0 0 1 0
1 0 0 1 0
0 0  0 0 0
1 0  0 0 0
0 65535 1 0 X
1 65535 1 0 X
0  0 0 0 0
1  0 0 0 0
0 65524 1 0 X
1 65524 1 0 X
0  0 0 0 X
1  0 0 0 65524
*/
