// Digital circuit 3.dig as structural Verilog
module _3 (
  input  [15:0] A,
  input  \input ,
  input  clk,
  input  reset,
  output [15:0] mean,
  output busy
);

  wire d_ff_1_q, d_ff_2_nq;
  wire [31:0] add_1_s, counter_1_out, d_ff_as_1_q;
  wire [31:16] div_1_q;

  D_FF d_ff_1 (.D(\input ), .C(clk), .Q(d_ff_1_q));  // open: nQ
  D_FF d_ff_2 (.D(d_ff_1_q), .C(clk), .nQ(d_ff_2_nq));  // open: Q
  Add #(.Bits(32)) add_1 (.a({{16{1'b0}}, A}), .b(d_ff_as_1_q), .c_i(busy), .s(add_1_s));  // open: c_o
  Counter #(.Bits(32)) counter_1 (.en(1'b1), .C(busy), .clr(reset), .out(counter_1_out));  // open: ovf
  and and_1 (busy, d_ff_1_q, d_ff_2_nq);
  D_FF_AS #(.Bits(32)) d_ff_as_1 (.Set(1'b0), .D(add_1_s), .C(busy), .Clr(reset), .Q(d_ff_as_1_q));  // open: nQ
  // Probe on d_ff_as_1_q
  Div #(.Bits(32)) div_1 (.a(d_ff_as_1_q), .b(counter_1_out), .q({div_1_q, mean}));  // open: r

  // Other names for the same wires on the sheet: A_t[15:0] = A; clr = reset; inp = busy
endmodule
