// Digital circuit counter.dig as structural Verilog
module counter (
  input  reset,
  input  clk,
  output A,
  output B,
  output C
);

  wire A_t, and_1_out, and_2_out, and_3_out, and_4_out, B_t, C_t, xor_1_out, xor_2_out;

  and and_1 (and_1_out, A_t, B_t);
  xor xor_1 (xor_1_out, A_t, B_t);
  xor xor_2 (xor_2_out, and_1_out, C_t);
  and and_2 (and_2_out, ~reset, ~A_t);  // And
  and and_3 (and_3_out, ~reset, xor_1_out);  // And
  and and_4 (and_4_out, ~reset, xor_2_out);  // And
  D_FF d_ff_1 (.D(and_2_out), .C(clk), .Q(A_t));  // open: nQ
  D_FF d_ff_2 (.D(and_3_out), .C(clk), .Q(B_t));  // open: nQ
  D_FF d_ff_3 (.D(and_4_out), .C(clk), .Q(C_t));  // open: nQ
  LookUpTable #(.Bits(3)) lookuptable_1 (.in0(A_t), .in1(B_t), .in2(C_t), .out({C, B, A}));

  // Notes on the sheet:
  //   contents of lookuptable_1 (hex, n*v repeats v):
  //   0,3,6,5,2,1,4,7
endmodule

/* Test case TestCase:
clk reset C B A
0 0 0 0 0 
0 1 0 0 0
1 1 0 0 0
0 0 0 0 0
1 0 0 1 1
0 0 0 1 1
1 0 1 1 0
0 0 1 1 0 
1 0 1 0 1
0 0 1 0 1
1 0 0 1 0
0 0 0 1 0
1 0 0 0 1
0 0 0 0 1
1 0 1 0 0
0 0 1 0 0
1 0 1 1 1
0 0 1 1 1
1 0 0 0 0
0 0 0 0 0
1 0 0 1 1
0 0 0 1 1
1 0 1 1 0
0 0 1 1 0 
1 0 1 0 1
0 0 1 0 1
1 0 0 1 0
0 0 0 1 0
1 0 0 0 1
0 0 0 0 1
1 0 1 0 0
0 0 1 0 0
1 0 1 1 1
0 0 1 1 1
*/
