// Digital circuit peak.dig as structural Verilog
module peak (
  input  [15:0] A,
  input  \input ,
  input  clk,
  input  reset,
  output [17:0] peak
);

  wire comparator_1_lt, hasinput, latch, m2, not_1_out, not_2_out, or_1_out, previnput, register_5_q;
  wire [15:0] register_3_q, register_4_q, register_7_q;
  wire [17:0] bitextender_1_out, bitextender_2_out, bitextender_3_out, cpeak, multiplexer_1_out,
       multiplexer_2_out, multiplexer_3_out, multiplexer_4_out, neg_1_out, neg_2_out, sub_1_s, sub_2_s;

  not not_1 (not_1_out, m2);
  and and_1 (hasinput, \input , ~previnput);  // And
  or or_1 (or_1_out, reset, not_1_out);
  Multiplexer #(.Bits(18)) multiplexer_1 (.sel(comparator_1_lt), .in_0(peak), .in_1(cpeak), .out(multiplexer_1_out));
  Comparator #(.Bits(18)) comparator_1 (.a(peak), .b(cpeak), .lt(comparator_1_lt));  // open: gt, eq
  or or_2 (latch, hasinput, reset);
  Multiplexer #(.Bits(18)) multiplexer_2 (
    .sel(or_1_out), .in_0(multiplexer_1_out), .in_1({18{1'b0}}), .out(multiplexer_2_out));
  Register #(.Bits(18)) register_1 (.D(multiplexer_2_out), .C(clk), .en(latch), .Q(peak));
  Register register_2 (.D(\input ), .C(clk), .en(1'b1), .Q(previnput));
  Register #(.Bits(16)) register_3 (.D(A), .C(clk), .en(latch), .Q(register_3_q));
  BitExtender #(.inputBits(16), .outputBits(18)) bitextender_1 (.in(A), .out(bitextender_1_out));
  not not_2 (not_2_out, reset);
  Register #(.Bits(16)) register_4 (.D(register_3_q), .C(clk), .en(latch), .Q(register_4_q));
  Register register_5 (.D(not_2_out), .C(clk), .en(latch), .Q(register_5_q));
  BitExtender #(.inputBits(16), .outputBits(18)) bitextender_2 (.in(register_3_q), .out(bitextender_2_out));
  Sub #(.Bits(18)) sub_1 (.a(bitextender_2_out), .b(bitextender_1_out), .c_i(1'b0), .s(sub_1_s));  // open: c_o
  Sub #(.Bits(18)) sub_2 (.a(bitextender_2_out), .b(bitextender_3_out), .c_i(1'b0), .s(sub_2_s));  // open: c_o
  Register register_6 (.D(register_5_q), .C(clk), .en(latch), .Q(m2));
  Register #(.Bits(16)) register_7 (.D(register_4_q), .C(clk), .en(latch), .Q(register_7_q));
  BitExtender #(.inputBits(16), .outputBits(18)) bitextender_3 (.in(register_4_q), .out(bitextender_3_out));
  Neg #(.Bits(18)) neg_1 (.in(sub_1_s), .out(neg_1_out));
  Neg #(.Bits(18)) neg_2 (.in(sub_2_s), .out(neg_2_out));
  Multiplexer #(.Bits(18)) multiplexer_3 (.sel(sub_1_s[17]), .in_0(sub_1_s), .in_1(neg_1_out), .out(multiplexer_3_out));
  Multiplexer #(.Bits(18)) multiplexer_4 (.sel(sub_2_s[17]), .in_0(sub_2_s), .in_1(neg_2_out), .out(multiplexer_4_out));
  Register register_8 (.D(m2), .C(clk), .en(latch));  // open: Q
  Add #(.Bits(18)) add_1 (.a(multiplexer_3_out), .b(multiplexer_4_out), .c_i(1'b0), .s(cpeak));  // open: c_o

  // Other names for the same wires on the sheet: Max[17:0] = peak

  // Notes on the sheet:
  //   clk: Hz: 200
endmodule

/* Test case Case1:
clk A input reset peak
0 0 0 0 0
1 0 0 0 0
0 0 0 1 0
1 0 0 1 0
0 0  0 0 0
1 0  0 0 0
0 5 1 0 X
1 5 1 0 X
0 0 0 0 X
1 0 0 0 X
0 1 1 0 X
1 1 1 0 X
0 0 0 0 X
1 0 0 0 X
0 0 0 0 X
1 0 0 0 X
0 2 1 0 X
1 2 1 0 X
0 0 0 0 X
1 0 0 0 X
0  0 0 0 5
1  0 0 0 5
0 10 1 0 X
1 10 1 0 X
0 0 0 0 X
1 0 0 0 9
0  0 0 0 9
1  0 0 0 9
0 3 1 0 X
1 3 1 0 X
0 0 0 0 X
1 0 0 0 15
0  0 0 0 15
1  0 0 0 15
0 65526 1 0 X
1 65526 1 0 X
0 0 0 0 X
1 0 0 0 20
0  0 0 0 20
1  0 0 0 20
0 2 1 0 X
1 2 1 0 X
0 0 0 0 X
1 0 0 0 25
0  0 0 0 25
1  0 0 0 25
0 4 1 0 X
1 4 1 0 X
0 0 0 0 X
1 0 0 0 25
0  0 0 0 25
1  0 0 0 25
0 1 1 0 X
1 1 1 0 X
0 0 0 0 X
1 0 0 0 25
0  0 0 0 25
1  0 0 0 25
0 2 1 0 X
1 2 1 0 X
0 0 0 0 X
1 0 0 0 25
*/
