// Digital circuit final_diglab_2024_cp_01-170015.dig as structural Verilog
module final_diglab_2024_cp_01_170015 (
  input  reset,
  input  clk,
  output A,
  output B,
  output C
);

  wire [2:0] counter_1_out;

  Counter #(.Bits(3)) counter_1 (.en(1'b1), .C(clk), .clr(reset), .out(counter_1_out));  // open: ovf
  Multiplexer #(.Bits(3), .Selector_Bits(3)) multiplexer_1 (
    .sel(counter_1_out), .in_0(3'b000), .in_1(3'b011), .in_2(3'b110), .in_3(3'b101), .in_4(3'b010),
    .in_5(3'b001), .in_6(3'b100), .in_7(3'b111), .out({C, B, A}));
endmodule
