// Digital circuit 02-01.dig as structural Verilog
module _02_01 (
  input  A,
  input  B,
  output Output
);

  wire and_1_out, and_2_out;

  and and_1 (and_1_out, ~A, B);  // And
  and and_2 (and_2_out, A, ~B);  // And
  or or_1 (Output, and_1_out, and_2_out);
endmodule
