// Digital circuit 02-04.dig as structural Verilog
module _02_04 (
  input  A,
  input  B,
  input  Cin
);

  wire not_1_out, not_2_out, not_3_out;

  not not_1 (not_1_out, A);
  not not_2 (not_2_out, B);
  not not_3 (not_3_out, Cin);
endmodule
