// Digital circuit 03-01.dig as structural Verilog
module _03_01 (
  input  [3:0] In,
  output A,
  output B,
  output C,
  output D,
  output E,
  output F,
  output G
);

  wire and_1_out, and_2_out, and_3_out, and_4_out, and_5_out, and_6_out, and_7_out, and_8_out, and_9_out,
       and_10_out, and_11_out, and_12_out, and_13_out, and_14_out, not_1_out, not_2_out, not_3_out;

  not not_1 (not_1_out, In[2]);
  not not_2 (not_2_out, In[1]);
  not not_3 (not_3_out, In[0]);
  and and_1 (and_1_out, not_3_out, not_1_out);
  and and_2 (and_2_out, In[0], In[2]);
  and and_3 (and_3_out, not_3_out, not_2_out);
  and and_4 (and_4_out, In[0], In[1]);
  or or_1 (C, In[0], not_2_out, In[2]);
  and and_5 (and_5_out, not_3_out, not_1_out);
  and and_6 (and_6_out, In[0], not_2_out, In[2]);
  and and_7 (and_7_out, not_3_out, In[1]);
  and and_8 (and_8_out, In[1], not_1_out);
  and and_9 (and_9_out, not_3_out, not_1_out);
  and and_10 (and_10_out, not_3_out, In[1]);
  and and_11 (and_11_out, not_3_out, not_2_out);
  and and_12 (and_12_out, not_3_out, In[1]);
  and and_13 (and_13_out, In[1], not_1_out);
  and and_14 (and_14_out, not_2_out, In[2]);
  or or_2 (B, and_3_out, and_4_out, not_1_out);
  or or_3 (E, and_9_out, and_10_out);
  or or_4 (F, and_11_out, In[2], In[3]);
  or or_5 (A, and_1_out, and_2_out, In[1], In[3]);
  or or_6 (D, and_5_out, and_6_out, and_7_out, and_8_out, In[3]);
  or or_7 (G, and_12_out, and_13_out, and_14_out, In[3]);
  Seven_Seg seven_seg_1 (.a(A), .b(B), .c(C), .d(D), .e(E), .f(F), .g(G), .dp(1'b0));

  // Other names for the same wires on the sheet: In_0 = In[0]; In_1 = In[1]; In_2 = In[2]; In_3 = In[3]
endmodule
