// Digital circuit 03-02.dig as structural Verilog
module _03_02 (
  input  [2:0] In,
  output A,
  output B,
  output C,
  output D,
  output E,
  output F,
  output G,
  output H,
  output [7:0] Z
);

  wire and_1_out, and_2_out, and_3_out, and_4_out, and_5_out, and_6_out, and_7_out, and_8_out, and_9_out,
       and_10_out, and_11_out, and_12_out, and_13_out, and_14_out, and_15_out, not_1_out, not_2_out,
       not_3_out;

  not not_1 (not_1_out, In[2]);
  not not_2 (not_2_out, In[1]);
  not not_3 (not_3_out, In[0]);
  and and_1 (and_1_out, In[0], not_2_out, not_1_out);
  and and_2 (and_2_out, not_3_out, In[1]);
  and and_3 (and_3_out, not_3_out, In[2]);
  and and_4 (and_4_out, In[1], In[2]);
  and and_5 (and_5_out, In[0], not_1_out);
  and and_6 (and_6_out, not_2_out, In[2]);
  and and_7 (and_7_out, not_3_out, not_2_out);
  and and_8 (and_8_out, In[1], not_1_out);
  and and_9 (and_9_out, not_2_out, In[2]);
  and and_10 (and_10_out, not_3_out, In[1], not_1_out);
  and and_11 (and_11_out, not_3_out, not_2_out, In[2]);
  and and_12 (and_12_out, In[0], In[1], In[2]);
  and and_13 (and_13_out, In[0], not_2_out, not_1_out);
  and and_14 (and_14_out, not_3_out, In[1]);
  and and_15 (and_15_out, not_3_out, In[2]);
  or or_1 (E, and_5_out, and_6_out);
  or or_2 (F, and_7_out, and_8_out, and_9_out);
  or or_3 (G, and_10_out, and_11_out, and_12_out);
  or or_4 (H, and_13_out, and_14_out, and_15_out);
  or or_5 (C, and_1_out, and_2_out, and_3_out, and_4_out);

  assign A = 1'b0;
  assign B = 1'b1;
  assign D = 1'b0;
  assign Z = {2'b01, C, 1'b0, E, F, G, H};

  // Other names for the same wires on the sheet: In_0 = In[0]; In_1 = In[1]; In_2 = In[2]
endmodule
