// Digital circuit 642-3.dig as structural Verilog
module _642_3 (
  output D3,
  output D2,
  output D1,
  output D0
);

  wire and_1_out, and_2_out, and_3_out, and_4_out, and_5_out, and_6_out, and_7_out, not_1_out, not_2_out,
       not_3_out, not_4_out, X1, X2, X3;

  not not_1 (not_1_out, X3);
  not not_2 (not_2_out, X2);
  not not_3 (not_3_out, X1);
  not not_4 (not_4_out, D0);
  and and_1 (and_1_out, X2, D0);
  and and_2 (and_2_out, X1, D0);
  and and_3 (and_3_out, not_2_out, not_3_out, D0);
  and and_4 (and_4_out, X2, X1);
  and and_5 (and_5_out, X2, not_4_out);
  and and_6 (and_6_out, X2, not_3_out, D0);
  and and_7 (and_7_out, X1, not_4_out);
  or or_1 (D3, and_1_out, X3, and_2_out);
  or or_2 (D2, and_3_out, and_4_out, and_5_out);
  or or_3 (D1, and_6_out, X3, and_7_out);

  // Other names for the same wires on the sheet: X0 = D0
endmodule
