// Digital circuit Cyclic.dig as structural Verilog
module Cyclic (
  output B3,
  output B2,
  output B1,
  output B0
);

  wire and_1_out, and_2_out, and_3_out, and_4_out, not_1_out, not_2_out, not_3_out, not_4_out, X0, X1, X2;

  not not_1 (not_1_out, B3);
  not not_2 (not_2_out, X2);
  not not_3 (not_3_out, X1);
  not not_4 (not_4_out, X0);
  and and_1 (and_1_out, X2, not_3_out);
  and and_2 (and_2_out, not_2_out, X1);
  and and_3 (and_3_out, X1, not_4_out);
  and and_4 (and_4_out, not_3_out, X0);
  or or_1 (B2, B3, X2);
  or or_2 (B1, and_1_out, and_2_out);
  or or_3 (B0, and_3_out, and_4_out);

  // Other names for the same wires on the sheet: X3 = B3
endmodule
