// Digital circuit Excess-3.dig as structural Verilog
module Excess_3 (
  input  X3,
  input  X2,
  input  X1,
  input  X0,
  output A,
  output B,
  output C,
  output D
);

  wire and_1_out, and_2_out, and_3_out, and_4_out, and_5_out, and_6_out, and_7_out, not_1_out, not_2_out;

  not not_1 (not_1_out, X2);
  not not_2 (not_2_out, X1);
  not not_3 (D, X0);
  and and_1 (and_1_out, X0, X2);
  and and_2 (and_2_out, X1, X2);
  and and_3 (and_3_out, X0, not_1_out);
  and and_4 (and_4_out, D, not_2_out, X2);
  and and_5 (and_5_out, X1, not_1_out);
  and and_6 (and_6_out, D, not_2_out);
  and and_7 (and_7_out, X0, X1);
  or or_1 (A, and_1_out, and_2_out, X3);
  or or_2 (B, and_3_out, and_4_out, and_5_out);
  or or_3 (C, and_6_out, and_7_out);
endmodule
