// Digital circuit 03-04.dig as structural Verilog
module _03_04 (
  input  [6:0] In,
  output [6:0] Output
);

  wire A1, A2, A3, A4, A5, A6, A7, not_1_out, not_2_out, not_3_out, S1, S2, S3;

  not not_1 (not_1_out, S1);
  not not_2 (not_2_out, S2);
  not not_3 (not_3_out, S3);
  and and_1 (A1, not_1_out, not_2_out, S3);
  and and_2 (A2, not_1_out, S2, not_3_out);
  and and_3 (A3, not_1_out, S2, S3);
  and and_4 (A4, S1, not_2_out, not_3_out);
  and and_5 (A5, S1, not_2_out, S3);
  and and_6 (A6, S1, S2, not_3_out);
  and and_7 (A7, S1, S2, S3);
  xor xor_1 (S1, In[3], In[2], In[1], In[0]);
  xor xor_2 (S2, In[5], In[4], In[1], In[0]);
  xor xor_3 (S3, In[6], In[4], In[2], In[0]);
  assign Output = {A1, A2, A3, A4, A5, A6, A7} ^ In;  // XOr xor_4, 7 bits wide

  // Other names for the same wires on the sheet: M4 = In[0]; M3 = In[1]; M2 = In[2]; P3 = In[3]; M1 = In[4];
  //   P2 = In[5]; P1 = In[6]
endmodule
