// Digital circuit 06x.dig as structural Verilog
module _06x (
  input  [3:0] A,
  input  [3:0] B,
  input  [2:0] S,
  input  M,
  input  C,
  output [3:0] F,
  output Cout
);

  wire add_1_c_o, add_2_c_o, add_3_c_o, add_4_c_o, add_5_c_o, add_6_c_o, cout_t;
  wire [3:0] add_1_s, add_2_s, add_3_s, add_4_s, add_5_s, add_6_s, and_1_out, and_2_out, mux0, mux1,
       nand_1_out, nor_1_out, not_1_out, not_2_out, not_3_out, or_1_out, xnor_1_out;

  assign not_1_out = ~A;  // Not not_1, 4 bits wide
  assign nand_1_out = ~(A & B);  // NAnd nand_1, 4 bits wide
  assign nor_1_out = ~(A | B);  // NOr nor_1, 4 bits wide
  assign xnor_1_out = ~(A ^ B);  // XNOr xnor_1, 4 bits wide
  assign and_1_out = A & B;  // And and_1, 4 bits wide
  assign or_1_out = A | B;  // Or or_1, 4 bits wide
  assign and_2_out = A & ~B;  // And and_2, 4 bits wide
  Multiplexer #(.Selector_Bits(3), .Bits(4)) multiplexer_1 (
    .sel(S), .in_0(not_1_out), .in_1(nand_1_out), .in_2(nor_1_out), .in_3(xnor_1_out), .in_4(and_1_out),
    .in_5(or_1_out), .in_6(and_2_out), .in_7(A), .out(mux0));
  assign not_2_out = ~B;  // Not not_2, 4 bits wide
  assign not_3_out = ~A;  // Not not_3, 4 bits wide
  Multiplexer #(.Bits(4)) multiplexer_2 (.sel(M), .in_0(mux0), .in_1(mux1), .out(F));
  Add #(.Bits(4)) add_1 (.a(A), .b(4'b0000), .c_i(C), .s(add_1_s), .c_o(add_1_c_o));
  Add #(.Bits(4)) add_2 (.a(A), .b(4'b1111), .c_i(C), .s(add_2_s), .c_o(add_2_c_o));
  Add #(.Bits(4)) add_3 (.a(A), .b(B), .c_i(C), .s(add_3_s), .c_o(add_3_c_o));
  Add #(.Bits(4)) add_4 (.a(A), .b(not_2_out), .c_i(C), .s(add_4_s), .c_o(add_4_c_o));
  Add #(.Bits(4)) add_5 (.a(not_3_out), .b(4'b0000), .c_i(C), .s(add_5_s), .c_o(add_5_c_o));
  Add #(.Bits(4)) add_6 (.a(4'b0000), .b(B), .c_i(C), .s(add_6_s), .c_o(add_6_c_o));
  Multiplexer multiplexer_3 (.sel(M), .in_0(1'b0), .in_1(cout_t), .out(Cout));
  Multiplexer #(.Selector_Bits(3), .Bits(4)) multiplexer_4 (
    .sel(S), .in_0(add_1_s), .in_1(add_2_s), .in_2(add_3_s), .in_3(add_4_s), .in_4(add_5_s), .in_5(add_6_s),
    .in_6({A[2:0], 1'b0}), .in_7({1'b0, A[3:1]}), .out(mux1));
  Multiplexer #(.Selector_Bits(3)) multiplexer_5 (
    .sel(S), .in_0(add_1_c_o), .in_1(add_2_c_o), .in_2(add_3_c_o), .in_3(add_4_c_o), .in_4(add_5_c_o),
    .in_5(add_6_c_o), .in_6(1'b0), .in_7(1'b0), .out(cout_t));

  // Notes on the sheet:
  //   mux for F
  //   mux for cout
endmodule
