// Digital circuit VendingMachine.dig as structural Verilog
module VendingMachine (
  input  P5,
  input  reset,
  input  clock,
  input  P10,
  input  P20,
  input  Pcoffee,
  input  Ptea,
  input  Pchange,
  input  Pnext,
  output [5:0] Balance,
  output CoffeeOut,
  output TeaOut,
  output [1:0] Change5,
  output [1:0] Change10,
  output [1:0] Change20
);

  wire and_1_out, and_2_out, and_3_out, and_11_out, comparator_1_gt, comparator_2_gt, comparator_3_gt,
       comparator_4_lt, comparator_5_lt, d_ff_5_q, d_ff_6_q, d_ff_7_q, d_ff_8_q, d_ff_9_q, d_ff_10_q,
       d_ff_11_q, d_ff_12_q, d_ff_13_q, d_ff_14_q, d_ff_15_q, d_ff_16_q, d_ff_17_q, d_ff_18_q, gt20, gt25,
       lt30, lt40, lt45, nor_1_out, or_2_out, rst_plus_ch, s5, s10, s20, sChange, sCoffee, sCoffeeOut, sNext,
       sTea, sTeaOut;
  wire [1:0] multiplexer_3_out, multiplexer_4_out, multiplexer_5_out;
  wire [3:0] arith_sel;
  wire [5:0] add_1_s, add_2_s, add_3_s, d_ff_1_q, div_1_q, div_1_r, div_2_q, div_2_r, div_3_q,
       multiplexer_1_out, sub_1_s, sub_2_s;
  wire [5:2] multiplexer_3_out_2, multiplexer_4_out_2, multiplexer_5_out_2;

  Comparator #(.Bits(6)) comparator_1 (.a(Balance), .b(6'b101101), .gt(comparator_1_gt));  // open: eq, lt
  Comparator #(.Bits(6)) comparator_2 (.a(Balance), .b(6'b101000), .gt(comparator_2_gt));  // open: eq, lt
  Comparator #(.Bits(6)) comparator_3 (.a(Balance), .b(6'b011110), .gt(comparator_3_gt));  // open: eq, lt
  Comparator #(.Bits(6)) comparator_4 (.a(Balance), .b(6'b011001), .lt(comparator_4_lt));  // open: gt, eq
  Comparator #(.Bits(6)) comparator_5 (.a(Balance), .b(6'b010100), .lt(comparator_5_lt));  // open: gt, eq
  not not_1 (lt45, comparator_1_gt);
  not not_2 (lt40, comparator_2_gt);
  not not_3 (lt30, comparator_3_gt);
  not not_4 (gt25, comparator_4_lt);
  not not_5 (gt20, comparator_5_lt);
  nor nor_1 (nor_1_out, TeaOut, CoffeeOut);
  Add #(.Bits(6)) add_1 (.a(Balance), .b(6'b000101), .c_i(1'b0), .s(add_1_s));  // open: c_o
  Add #(.Bits(6)) add_2 (.a(Balance), .b(6'b001010), .c_i(1'b0), .s(add_2_s));  // open: c_o
  Add #(.Bits(6)) add_3 (.a(Balance), .b(6'b010100), .c_i(1'b0), .s(add_3_s));  // open: c_o
  Sub #(.Bits(6)) sub_1 (.a(Balance), .b(6'b011001), .c_i(1'b0), .s(sub_1_s));  // open: c_o
  Sub #(.Bits(6)) sub_2 (.a(Balance), .b(6'b010100), .c_i(1'b0), .s(sub_2_s));  // open: c_o
  and and_1 (and_1_out, lt45, nor_1_out, s5);
  and and_2 (and_2_out, lt40, nor_1_out, s10);
  and and_3 (and_3_out, lt30, nor_1_out, s20);
  and and_4 (sCoffeeOut, gt25, nor_1_out, sCoffee);
  and and_5 (sTeaOut, gt20, nor_1_out, sTea);
  // Probe on add_1_s
  // Probe on add_2_s
  // Probe on add_3_s
  // Probe on sub_1_s
  // Probe on sub_2_s
  LookUpTable #(.Bits(4)) lookuptable_1 (
    .in0(and_1_out), .in1(and_2_out), .in2(and_3_out), .in3(sCoffeeOut), .in4(sTeaOut), .out(arith_sel));
  Multiplexer #(.Bits(6), .Selector_Bits(4)) multiplexer_1 (
    .sel(arith_sel), .in_0(Balance), .in_1(add_1_s), .in_2(add_2_s), .in_3(add_3_s), .in_4(sub_1_s),
    .in_5(sub_2_s), .in_6(Balance), .in_7(Balance), .in_8(Balance), .in_9(Balance), .in_10(Balance),
    .in_11(Balance), .in_12(Balance), .in_13(Balance), .in_14(Balance), .in_15(Balance),
    .out(multiplexer_1_out));
  // Probe on arith_sel
  D_FF #(.Bits(6)) d_ff_1 (.D(multiplexer_1_out), .C(clock), .Q(d_ff_1_q));  // open: nQ
  Multiplexer #(.Bits(6)) multiplexer_2 (.sel(rst_plus_ch), .in_0(d_ff_1_q), .in_1({6{1'b0}}), .out(Balance));
  or or_1 (rst_plus_ch, reset, sChange);
  Div #(.Bits(6)) div_1 (.a(Balance), .b(6'b010100), .q(div_1_q), .r(div_1_r));
  Multiplexer #(.Bits(6)) multiplexer_3 (
    .sel(sChange), .in_0({6{1'b0}}), .in_1(div_1_q), .out({multiplexer_3_out_2, multiplexer_3_out}));
  Div #(.Bits(6)) div_2 (.a(div_1_r), .b(6'b001010), .q(div_2_q), .r(div_2_r));
  Multiplexer #(.Bits(6)) multiplexer_4 (
    .sel(sChange), .in_0({6{1'b0}}), .in_1(div_2_q), .out({multiplexer_4_out_2, multiplexer_4_out}));
  Div #(.Bits(6)) div_3 (.a(div_2_r), .b(6'b000101), .q(div_3_q));  // open: r
  Multiplexer #(.Bits(6)) multiplexer_5 (
    .sel(sChange), .in_0({6{1'b0}}), .in_1(div_3_q), .out({multiplexer_5_out_2, multiplexer_5_out}));
  D_FF #(.Bits(2)) d_ff_2 (.D(multiplexer_3_out), .C(rst_plus_ch), .Q(Change20));  // open: nQ
  D_FF #(.Bits(2)) d_ff_3 (.D(multiplexer_4_out), .C(rst_plus_ch), .Q(Change10));  // open: nQ
  D_FF #(.Bits(2)) d_ff_4 (.D(multiplexer_5_out), .C(rst_plus_ch), .Q(Change5));  // open: nQ
  D_FF d_ff_5 (.D(P5), .C(clock), .Q(d_ff_5_q));  // open: nQ
  D_FF d_ff_6 (.D(P10), .C(clock), .Q(d_ff_6_q));  // open: nQ
  D_FF d_ff_7 (.D(P20), .C(clock), .Q(d_ff_7_q));  // open: nQ
  D_FF d_ff_8 (.D(Pcoffee), .C(clock), .Q(d_ff_8_q));  // open: nQ
  D_FF d_ff_9 (.D(Ptea), .C(clock), .Q(d_ff_9_q));  // open: nQ
  D_FF d_ff_10 (.D(Pchange), .C(clock), .Q(d_ff_10_q));  // open: nQ
  D_FF d_ff_11 (.D(Pnext), .C(clock), .Q(d_ff_11_q));  // open: nQ
  D_FF d_ff_12 (.D(d_ff_5_q), .C(clock), .Q(d_ff_12_q));  // open: nQ
  D_FF d_ff_13 (.D(d_ff_6_q), .C(clock), .Q(d_ff_13_q));  // open: nQ
  D_FF d_ff_14 (.D(d_ff_7_q), .C(clock), .Q(d_ff_14_q));  // open: nQ
  D_FF d_ff_15 (.D(d_ff_8_q), .C(clock), .Q(d_ff_15_q));  // open: nQ
  D_FF d_ff_16 (.D(d_ff_9_q), .C(clock), .Q(d_ff_16_q));  // open: nQ
  D_FF d_ff_17 (.D(d_ff_10_q), .C(clock), .Q(d_ff_17_q));  // open: nQ
  D_FF d_ff_18 (.D(d_ff_11_q), .C(clock), .Q(d_ff_18_q));  // open: nQ
  and and_6 (s5, d_ff_5_q, ~d_ff_12_q);  // And
  and and_7 (s10, d_ff_6_q, ~d_ff_13_q);  // And
  and and_8 (s20, d_ff_7_q, ~d_ff_14_q);  // And
  and and_9 (sCoffee, d_ff_8_q, ~d_ff_15_q);  // And
  and and_10 (sTea, d_ff_9_q, ~d_ff_16_q);  // And
  and and_11 (and_11_out, d_ff_10_q, ~d_ff_17_q);  // And
  and and_12 (sNext, d_ff_11_q, ~d_ff_18_q);  // And
  D_FF d_ff_19 (.D(and_11_out), .C(clock), .Q(sChange));  // open: nQ
  or or_2 (or_2_out, reset, sNext, sChange);
  RS_FF rs_ff_1 (.S(sCoffeeOut), .C(clock), .R(or_2_out), .Q(CoffeeOut));  // open: nQ
  RS_FF rs_ff_2 (.S(sTeaOut), .C(clock), .R(or_2_out), .Q(TeaOut));  // open: nQ

  // Other names for the same wires on the sheet: bal[5:0] = Balance; ch5[1:0] = Change5; ch10[1:0] = Change10;
  //   ch20[1:0] = Change20; clk = clock; coffee = CoffeeOut; rst = reset; tea = TeaOut

  // Notes on the sheet:
  //   contents of lookuptable_1 (hex, n*v repeats v):
  //   0,1,2,0,3,0,0,0,4,7*0,5
endmodule
