// Digital circuit 38decoder.dig as structural Verilog
module _38decoder (
  input  S2,
  input  S1,
  input  S0,
  output O1,
  output O2
);

  wire decoder_1_out_0, decoder_1_out_1, decoder_1_out_2, decoder_1_out_3, decoder_1_out_4, decoder_1_out_5,
       decoder_1_out_6, decoder_1_out_7;

  Decoder #(.Selector_Bits(3)) decoder_1 (
    .sel({S0, S1, S2}), .out_0(decoder_1_out_0), .out_1(decoder_1_out_1), .out_2(decoder_1_out_2),
    .out_3(decoder_1_out_3), .out_4(decoder_1_out_4), .out_5(decoder_1_out_5), .out_6(decoder_1_out_6),
    .out_7(decoder_1_out_7));
  or or_1 (O1, decoder_1_out_6, decoder_1_out_5, decoder_1_out_4, decoder_1_out_2);
  or or_2 (O2, decoder_1_out_7, decoder_1_out_6, decoder_1_out_4, decoder_1_out_2, decoder_1_out_0);
endmodule
