// Digital circuit 3bitsAddition.dig as structural Verilog
module _3bitsAddition (
  input  in_1,
  input  in_2,
  input  in_3,
  input  in_4,
  input  in_5,
  input  in_6
);

  wire [0:0] comparator_1_gt;
  wire [2:0] add_1_s;
  wire [3:3] add_1_c_o;

  Add #(.Bits(3)) add_1 (.a({in_1, in_2, in_3}), .b({in_4, in_5, in_6}), .c_i(1'b0), .s(add_1_s), .c_o(add_1_c_o[3]));
  Comparator #(.Bits(4)) comparator_1 (
    .a({add_1_c_o[3], add_1_s}), .b(4'b0110), .gt(comparator_1_gt[0]));  // open: eq, lt
  Seven_Seg_Hex seven_seg_hex_1 (.d({3'b000, comparator_1_gt[0]}), .dp(1'b0));
endmodule
