// Digital circuit diglab_2024_midterm_01-145441.dig as structural Verilog
module diglab_2024_midterm_01_145441 (
  input  [3:0] in,
  output out1,
  output out2
);

  LookUpTable lookuptable_1 (.in0(in[0]), .in1(in[1]), .in2(in[2]), .in3(in[3]), .out(out1));
  LookUpTable lookuptable_2 (.in0(in[0]), .in1(in[1]), .in2(in[2]), .in3(in[3]), .out(out2));

  // Notes on the sheet:
  //   contents of lookuptable_1 (hex, n*v repeats v):
  //   0,1,1,0,0,1,0,0,0,1,1,0,0,1,1
  //   contents of lookuptable_2 (hex, n*v repeats v):
  //   1,0,0,1,1,0,4*1,0,1,1,0,0,1
endmodule
