// Digital circuit diglab_2024_midterm_02-174604 (1).dig as structural Verilog
module diglab_2024_midterm_02_174604__1 (
  input  [7:0] in,
  output [2:0] out
);

  wire not_1_out, not_2_out, not_3_out;
  wire [2:0] lookuptable_1_out, priorityencoder_1_num, priorityencoder_2_num;

  PriorityEncoder #(.Selector_Bits(3)) priorityencoder_1 (
    .in0(in[0]), .in1(in[1]), .in2(in[2]), .in3(in[3]), .in4(in[4]), .in5(in[5]), .in6(in[6]), .in7(in[7]),
    .num(priorityencoder_1_num));  // open: any
  PriorityEncoder #(.Selector_Bits(3)) priorityencoder_2 (
    .in0(in[7]), .in1(in[6]), .in2(in[5]), .in3(in[4]), .in4(in[3]), .in5(in[2]), .in6(in[1]), .in7(in[0]),
    .num(priorityencoder_2_num));  // open: any
  not not_1 (not_1_out, priorityencoder_2_num[0]);
  not not_2 (not_2_out, priorityencoder_2_num[1]);
  not not_3 (not_3_out, priorityencoder_2_num[2]);
  // Probe on priorityencoder_1_num
  LookUpTable #(.Bits(3)) lookuptable_1 (.in0(not_1_out), .in1(not_2_out), .in2(not_3_out), .out(lookuptable_1_out));
  Sub #(.Bits(3)) sub_1 (.a(priorityencoder_1_num), .b(lookuptable_1_out), .c_i(1'b0), .s(out));  // open: c_o
  // Probe on lookuptable_1_out

  // Other names for the same wires on the sheet: o[2:0] = out

  // Notes on the sheet:
  //   contents of lookuptable_1 (hex, n*v repeats v):
  //   0,1,2,3,4,5,6
endmodule
