// Digital circuit diglab_2024_midterm_02-174904.dig as structural Verilog
module diglab_2024_midterm_02_174904 (
  input  [7:0] in,
  output [2:0] out
);

  wire and_1_out, and_2_out, and_3_out, and_4_out, and_5_out, and_6_out, and_7_out, and_8_out, and_9_out,
       and_10_out, and_11_out, and_12_out, and_13_out, and_14_out, and_15_out, and_16_out, and_17_out,
       and_18_out, and_19_out, and_20_out, and_21_out, and_22_out, and_23_out, and_24_out, and_25_out,
       and_26_out, and_27_out, and_28_out, and_29_out, and_30_out, and_31_out, and_32_out, and_33_out,
       and_34_out, and_35_out, and_36_out, and_37_out, and_38_out, and_39_out, and_40_out, not_1_out,
       not_2_out, not_3_out, not_4_out, not_5_out, not_6_out, not_7_out, not_8_out;

  not not_1 (not_1_out, in[7]);
  not not_2 (not_2_out, in[6]);
  not not_3 (not_3_out, in[5]);
  not not_4 (not_4_out, in[4]);
  not not_5 (not_5_out, in[3]);
  not not_6 (not_6_out, in[2]);
  not not_7 (not_7_out, in[1]);
  not not_8 (not_8_out, in[0]);
  and and_1 (and_1_out, in[0], in[4]);
  and and_2 (and_2_out, in[0], in[5]);
  and and_3 (and_3_out, in[0], in[6]);
  and and_4 (and_4_out, in[0], in[7]);
  and and_5 (and_5_out, in[1], in[5]);
  and and_6 (and_6_out, in[1], in[6]);
  and and_7 (and_7_out, in[1], in[7]);
  and and_8 (and_8_out, in[2], in[6]);
  and and_9 (and_9_out, in[2], in[7]);
  and and_10 (and_10_out, in[3], in[7]);
  and and_11 (and_11_out, not_8_out, not_7_out, not_6_out, in[3], in[5], not_1_out);
  and and_12 (and_12_out, not_8_out, not_7_out, in[2], in[4], not_2_out, not_1_out);
  and and_13 (and_13_out, not_8_out, not_7_out, in[2], in[5], not_2_out, not_1_out);
  and and_14 (and_14_out, not_8_out, in[1], in[3], not_3_out, not_2_out);
  and and_15 (and_15_out, not_8_out, in[1], in[4], not_3_out, not_2_out);
  and and_16 (and_16_out, in[0], in[2], not_4_out, not_3_out);
  and and_17 (and_17_out, in[0], in[3], not_4_out, not_3_out);
  and and_18 (and_18_out, in[0], in[6]);
  and and_19 (and_19_out, in[0], in[7]);
  and and_20 (and_20_out, not_7_out, not_6_out, not_5_out, in[4], in[6]);
  and and_21 (and_21_out, not_7_out, not_6_out, in[3], in[6], not_1_out);
  and and_22 (and_22_out, in[1], in[7]);
  and and_23 (and_23_out, not_6_out, not_5_out, in[4], in[7]);
  and and_24 (and_24_out, not_6_out, not_5_out, in[5], in[7]);
  and and_25 (and_25_out, not_8_out, in[1], in[2], not_5_out, not_3_out, not_1_out);
  and and_26 (and_26_out, not_8_out, not_6_out, in[3], in[4], not_3_out, not_1_out);
  and and_27 (and_27_out, not_8_out, not_6_out, not_4_out, in[5], in[6], not_1_out);
  and and_28 (and_28_out, in[0], in[1], not_6_out, not_4_out, not_2_out);
  and and_29 (and_29_out, not_8_out, in[1], in[4], not_3_out, not_1_out);
  and and_30 (and_30_out, not_8_out, not_6_out, in[3], in[6], not_1_out);
  and and_31 (and_31_out, not_8_out, in[1], in[6], not_1_out);
  and and_32 (and_32_out, in[0], in[3], not_4_out, not_2_out);
  and and_33 (and_33_out, in[0], in[5], not_2_out);
  and and_34 (and_34_out, in[0], in[7]);
  and and_35 (and_35_out, not_7_out, in[2], in[3], not_4_out, not_2_out);
  and and_36 (and_36_out, not_7_out, not_5_out, in[4], in[5], not_2_out);
  and and_37 (and_37_out, not_7_out, not_5_out, not_3_out, in[6], in[7]);
  and and_38 (and_38_out, not_7_out, in[2], in[5], not_2_out);
  and and_39 (and_39_out, not_7_out, not_5_out, in[4], in[7]);
  and and_40 (and_40_out, not_7_out, in[2], in[7]);
  or or_1 (out[2], and_1_out, and_2_out, and_3_out, and_4_out, and_5_out, and_6_out, and_7_out, and_8_out, and_9_out, and_10_out);
  or or_2 (out[1], and_11_out, and_12_out, and_13_out, and_14_out, and_15_out, and_16_out, and_17_out, and_18_out, and_19_out, and_20_out, and_21_out, and_22_out, and_23_out, and_24_out);
  or or_3 (out[0], and_25_out, and_26_out, and_27_out, and_28_out, and_29_out, and_30_out, and_31_out, and_32_out, and_33_out, and_34_out, and_35_out, and_36_out, and_37_out, and_38_out, and_39_out, and_40_out);

  // Other names for the same wires on the sheet: in_0 = in[0]; in_1 = in[1]; in_2 = in[2]; in_3 = in[3]; in_4 = in[4];
  //   in_5 = in[5]; in_6 = in[6]; in_7 = in[7]; out_0 = out[0]; out_1 = out[1]; out_2 = out[2]
endmodule
